// Logisim project ALaw.circ as structural Verilog
module Linear2ALaw (
);

  wire CLK, clock_1_out, LOAD, or_1_out, RST, s_r_ff_1_q, SHIFT, SIGN, STOP, undriven;
  wire [2:0] priority_encoder_1_out, SEG;
  wire [3:0] adder_1_out, bit_extender_1_out, counter_1_q, dipswitch_1_sw10, dipswitch_1_sw14;
  wire [7:0] ALAW, undriven_2;
  wire [12:8] dipswitch_1_sw6;
  wire [13:0] demultiplexer_1_out0, demultiplexer_1_out1, LINEAR, xor_1_out;

  Hex_Digit_Display hex_digit_display_1 (.value({2'b00, SIGN, dipswitch_1_sw6[12]}));  // open: dp
  Clock clock_1 (.out(clock_1_out));
  S_R_Flip_Flop s_r_ff_1 (.S(LOAD), .R(STOP), .clk(clock_1_out), .Q(s_r_ff_1_q));  // open: reset, Qn, preset
  Hex_Digit_Display hex_digit_display_2 (.value(dipswitch_1_sw6[11:8]));  // open: dp
  Hex_Digit_Display hex_digit_display_3 (.value(dipswitch_1_sw10));  // open: dp
  Hex_Digit_Display hex_digit_display_4 (.value(ALAW[7:4]));  // open: dp
  and and_1 (CLK, clock_1_out, s_r_ff_1_q);
  Hex_Digit_Display hex_digit_display_5 (.value(dipswitch_1_sw14));  // open: dp
  DipSwitch #(.number(14)) dipswitch_1 (
    .sw1(SIGN), .sw2(dipswitch_1_sw6[12]), .sw3(dipswitch_1_sw6[11]), .sw4(dipswitch_1_sw6[10]),
    .sw5(dipswitch_1_sw6[9]), .sw6(dipswitch_1_sw6[8]), .sw7(dipswitch_1_sw10[3]), .sw8(dipswitch_1_sw10[2]),
    .sw9(dipswitch_1_sw10[1]), .sw10(dipswitch_1_sw10[0]), .sw11(dipswitch_1_sw14[3]),
    .sw12(dipswitch_1_sw14[2]), .sw13(dipswitch_1_sw14[1]), .sw14(dipswitch_1_sw14[0]));
  DotMatrix #(.matrixcols(8), .matrixrows(1)) dotmatrix_1 (
    .col0(ALAW[7]), .col1(ALAW[6]), .col2(ALAW[5]), .col3(ALAW[4]), .col4(ALAW[3]), .col5(ALAW[2]),
    .col6(ALAW[1]), .col7(ALAW[0]));
  Hex_Digit_Display hex_digit_display_6 (.value(ALAW[3:0]));  // open: dp
  Button button_1 (.out(LOAD));
  Button button_2 (.out(RST));
  Demultiplexer #(.width(14), .enable("false")) demultiplexer_1 (
    .out0(demultiplexer_1_out0), .out1(demultiplexer_1_out1),
    .in({SIGN, dipswitch_1_sw6, dipswitch_1_sw10, dipswitch_1_sw14}), .sel(SIGN));
  Counter #(.width(4), .max('hf)) counter_1 (
    .clr(or_1_out), .clk(CLK), .Q(counter_1_q));  // open: load, up, count, D, carry
  or or_1 (or_1_out, RST, LOAD);
  Priority_Encoder priority_encoder_1 (
    .in0(LINEAR[5]), .in1(LINEAR[6]), .in2(LINEAR[7]), .in3(LINEAR[8]), .in4(LINEAR[9]), .in5(LINEAR[10]),
    .in6(LINEAR[11]), .in7(LINEAR[12]), .out(priority_encoder_1_out), .en_in(1'b1));
  assign xor_1_out = demultiplexer_1_out1 ^ {14{1'b1}};  // XOR_Gate xor_1, 14 bits wide
  Multiplexer #(.width(3), .enable("false")) multiplexer_1 (
    .in0(priority_encoder_1_out), .in1(3'b000), .out(SEG), .sel(undriven));
  Multiplexer #(.width(14), .enable("false")) multiplexer_2 (
    .in0(demultiplexer_1_out0), .in1(xor_1_out), .out(LINEAR), .sel(SIGN));
  Hex_Digit_Display hex_digit_display_7 (.value(bit_extender_1_out));  // open: dp
  assign bit_extender_1_out = {{1{1'b0}}, SEG};  // Bit_Extender bit_extender_1
  Adder #(.width(4)) adder_1 (.a(bit_extender_1_out), .b(4'b0001), .out(adder_1_out));  // open: cin, cout
  // Shift_Register #(.length(13)) shift_register_1: pin names not known; wires that end beside it: RST, LOAD, SHIFT, CLK, 1'b0, LINEAR[12], LINEAR[11], LINEAR[10], LINEAR[9], LINEAR[8], LINEAR[7], LINEAR[6], LINEAR[5], LINEAR[4], LINEAR[3], LINEAR[2], LINEAR[1], undriven_2[3], undriven_2[2], undriven_2[1]
  Comparator #(.width(4), .mode("unsigned")) comparator_1 (
    .a(counter_1_q), .b(adder_1_out), .eq(STOP));  // open: gt, lt
  not not_1 (SHIFT, STOP);
  not not_2 (undriven_2[7], SIGN);
  assign ALAW = {undriven_2[7], SEG, undriven_2[3:0]} ^ 8'h55;  // XOR_Gate xor_2, 8 bits wide

  // Other names for the same wires on the sheet: START = LOAD

  // Notes on the sheet:
  //   CLOCK GENERATION
  //   µ-Law Output
  //   LINEAR INPUT
  //   1's Complement
  //   MAGNITUDE CALCULATION
  //   START / STOP STATE MACHINE
  //   LINEAR VALUE RIGHT SHIFT
endmodule
