// Logisim project CW_Sender.circ as structural Verilog: 1 circuit, main circuit main
module main (
);

  wire CLK, clock_1_out, counter_1_carry, j_k_ff_1_q, multiplexer_1_out, START_out;
  wire [7:0] rom_1_data;
  wire [14:0] counter_1_q;

  Button START (.out(START_out));
  Clock clock_1 (.out(clock_1_out));
  J_K_Flip_Flop j_k_ff_1 (
    .J(START_out), .K(counter_1_carry), .clk(clock_1_out), .Q(j_k_ff_1_q));  // open: Qn, preset, reset
  and and_1 (CLK, j_k_ff_1_q, clock_1_out);
  Counter #(.max('h7fff), .ongoal("stay"), .width(15)) counter_1 (
    .clr(START_out), .up(1'b1), .clk(CLK), .carry(counter_1_carry), .Q(counter_1_q));  // open: load, count, D
  ROM #(.addrWidth(12)) rom_1 (.addr(counter_1_q[14:3]), .data(rom_1_data));
  Multiplexer #(.enable("false"), .select(3)) multiplexer_1 (
    .in0(rom_1_data[0]), .in1(rom_1_data[1]), .in2(rom_1_data[2]), .in3(rom_1_data[3]), .in4(rom_1_data[4]),
    .in5(rom_1_data[5]), .in6(rom_1_data[6]), .in7(rom_1_data[7]), .out(multiplexer_1_out),
    .sel(counter_1_q[2:0]));
  LED led_1 (.in(multiplexer_1_out));

  // Notes on the sheet:
  //   contents of rom_1 (hex, n*v repeats v):
  //   eb ae ee b8
endmodule
