// Logisim project Linear2muLaw.circ as structural Verilog: 1 circuit, main circuit main
module main (
);

  wire CLK, clock_1_out, CLR, comparator_1_lt, LOAD, or_1_out, RST, s_r_ff_1_q, SHIFT, START, STOP, undriven;
  wire [2:0] priority_encoder_1_out;
  wire [3:0] adder_1_out, bit_extender_1_out, counter_1_q, dipswitch_1_sw10, dipswitch_1_sw14, not_1_out;
  wire [7:0] MULAW;
  wire [12:8] dipswitch_1_sw6;
  wire [13:0] demultiplexer_1_out0, demultiplexer_1_out1, LINEAR, multiplexer_2_out, multiplexer_3_out,
       negator_1_out;

  Hex_Digit_Display hex_digit_display_1 (.value({2'b00, MULAW[7], dipswitch_1_sw6[12]}));  // open: dp
  Clock clock_1 (.out(clock_1_out));
  S_R_Flip_Flop s_r_ff_1 (.S(START), .R(STOP), .clk(clock_1_out), .Q(s_r_ff_1_q));  // open: reset, Qn, preset
  Hex_Digit_Display hex_digit_display_2 (.value(dipswitch_1_sw6[11:8]));  // open: dp
  Hex_Digit_Display hex_digit_display_3 (.value(dipswitch_1_sw10));  // open: dp
  Hex_Digit_Display hex_digit_display_4 (.value(MULAW[3:0]));  // open: dp
  Hex_Digit_Display hex_digit_display_5 (.value(MULAW[7:4]));  // open: dp
  and and_1 (CLK, clock_1_out, s_r_ff_1_q);
  Hex_Digit_Display hex_digit_display_6 (.value(dipswitch_1_sw14));  // open: dp
  DipSwitch #(.number(14)) dipswitch_1 (
    .sw1(MULAW[7]), .sw2(dipswitch_1_sw6[12]), .sw3(dipswitch_1_sw6[11]), .sw4(dipswitch_1_sw6[10]),
    .sw5(dipswitch_1_sw6[9]), .sw6(dipswitch_1_sw6[8]), .sw7(dipswitch_1_sw10[3]), .sw8(dipswitch_1_sw10[2]),
    .sw9(dipswitch_1_sw10[1]), .sw10(dipswitch_1_sw10[0]), .sw11(dipswitch_1_sw14[3]),
    .sw12(dipswitch_1_sw14[2]), .sw13(dipswitch_1_sw14[1]), .sw14(dipswitch_1_sw14[0]));
  DotMatrix #(.matrixcols(8), .matrixrows(1)) dotmatrix_1 (
    .col0(MULAW[7]), .col1(MULAW[6]), .col2(MULAW[5]), .col3(MULAW[4]), .col4(MULAW[3]), .col5(MULAW[2]),
    .col6(MULAW[1]), .col7(MULAW[0]));
  Button button_1 (.out(START));
  Button button_2 (.out(RST));
  Demultiplexer #(.width(14), .enable("false")) demultiplexer_1 (
    .out0(demultiplexer_1_out0), .out1(demultiplexer_1_out1),
    .in({MULAW[7], dipswitch_1_sw6, dipswitch_1_sw10, dipswitch_1_sw14}), .sel(MULAW[7]));
  Counter #(.width(4), .max('hf)) counter_1 (
    .clr(or_1_out), .clk(CLK), .Q(counter_1_q));  // open: load, up, count, D, carry
  or or_1 (or_1_out, RST, START);
  Priority_Encoder priority_encoder_1 (
    .in0(LINEAR[5]), .in1(LINEAR[6]), .in2(LINEAR[7]), .in3(LINEAR[8]), .in4(LINEAR[9]), .in5(LINEAR[10]),
    .in6(LINEAR[11]), .in7(LINEAR[12]), .out(priority_encoder_1_out), .en_in(1'b1));
  Negator #(.width(14)) negator_1 (.in(demultiplexer_1_out1), .out(negator_1_out));
  Multiplexer #(.width(3), .enable("false")) multiplexer_1 (
    .in0(priority_encoder_1_out), .in1(3'b000), .out(MULAW[6:4]), .sel(undriven));
  Multiplexer #(.width(14), .enable("false")) multiplexer_2 (
    .in0(demultiplexer_1_out0), .in1(negator_1_out), .out(multiplexer_2_out), .sel(MULAW[7]));
  Hex_Digit_Display hex_digit_display_7 (.value(bit_extender_1_out));  // open: dp
  assign bit_extender_1_out = {{1{1'b0}}, MULAW[6:4]};  // Bit_Extender bit_extender_1
  Comparator #(.width(14)) comparator_1 (.a(14'h1fdf), .b(multiplexer_2_out), .lt(comparator_1_lt));  // open: gt, eq
  Multiplexer #(.width(14), .enable("false")) multiplexer_3 (
    .in0(multiplexer_2_out), .in1(14'h1fdf), .out(multiplexer_3_out), .sel(comparator_1_lt));
  assign not_1_out = ~counter_1_q;  // NOT_Gate not_1, 4 bits wide
  Adder #(.width(4)) adder_1 (.a(bit_extender_1_out), .b(4'b0011), .out(adder_1_out));  // open: cin, cout
  Adder #(.width(14)) adder_2 (.a(multiplexer_3_out), .b(14'h21), .out(LINEAR));  // open: cin, cout
  Comparator #(.width(4), .mode("unsigned")) comparator_2 (
    .a(counter_1_q), .b(adder_1_out), .eq(STOP));  // open: gt, lt
  and and_2 (LOAD, not_1_out[3], not_1_out[2], not_1_out[1], counter_1_q[0]);
  and and_3 (CLR, not_1_out[3], not_1_out[2], not_1_out[1], not_1_out[0]);
  // Shift_Register #(.length(13)) shift_register_1: pin names not known; wires that end beside it: CLR, LOAD, SHIFT, CLK, 1'b0, LINEAR[12], LINEAR[11], LINEAR[10], LINEAR[9], LINEAR[8], LINEAR[7], LINEAR[6], LINEAR[5], LINEAR[4], LINEAR[3], LINEAR[2], LINEAR[1], MULAW[3], MULAW[2], MULAW[1]
  nor nor_1 (SHIFT, STOP, LOAD, CLR);

  // Other names for the same wires on the sheet: SEG[2:0] = MULAW[6:4]; SIGN = MULAW[7]

  // Notes on the sheet:
  //   CLOCK GENERATION
  //   LINEAR INPUT
  //   µ-Law Output
  //   MAGNITUDE CALCULATION
  //   START / STOP STATE MACHINE
  //   LINEAR VALUE RIGHT SHIFT
endmodule
