// Logisim project MuLaw2Linear.circ as structural Verilog: 1 circuit, main circuit main
module main (
);

  wire CLK, clock_1_out, CLR, LOAD, or_1_out, RST, s_r_ff_1_q, SHIFT, START, STOP;
  wire [3:0] adder_1_out, bit_extender_1_out, counter_1_q, not_1_out;
  wire [5:0] adder_2_out;
  wire [7:0] MULAW;
  wire [12:0] shift_register_1_p13;
  wire [13:0] demultiplexer_1_out0, demultiplexer_1_out1, LINEAR, negator_1_out, subtractor_1_out;

  Hex_Digit_Display hex_digit_display_1 (.value(MULAW[7:4]));  // open: dp
  Clock clock_1 (.out(clock_1_out));
  S_R_Flip_Flop s_r_ff_1 (.S(START), .R(STOP), .clk(clock_1_out), .Q(s_r_ff_1_q));  // open: reset, Qn, preset
  Hex_Digit_Display hex_digit_display_2 (.value(MULAW[3:0]));  // open: dp
  DipSwitch dipswitch_1 (
    .sw1(MULAW[7]), .sw2(MULAW[6]), .sw3(MULAW[5]), .sw4(MULAW[4]), .sw5(MULAW[3]), .sw6(MULAW[2]),
    .sw7(MULAW[1]), .sw8(MULAW[0]));
  or or_1 (or_1_out, RST, START);
  and and_1 (CLK, clock_1_out, s_r_ff_1_q);
  Counter #(.width(4), .max('hf)) counter_1 (
    .clr(or_1_out), .clk(CLK), .Q(counter_1_q));  // open: load, up, count, D, carry
  Hex_Digit_Display hex_digit_display_3 (.value({2'b00, LINEAR[13:12]}));  // open: dp
  Hex_Digit_Display hex_digit_display_4 (.value(LINEAR[11:8]));  // open: dp
  Hex_Digit_Display hex_digit_display_5 (.value(LINEAR[7:4]));  // open: dp
  assign bit_extender_1_out = {{1{1'b0}}, MULAW[6:4]};  // Bit_Extender bit_extender_1
  Adder #(.width(4)) adder_1 (.a(bit_extender_1_out), .b(4'b0010), .out(adder_1_out));  // open: cin, cout
  Button u_START (.out(START));
  Button u_RST (.out(RST));
  DotMatrix #(.matrixcols(14), .matrixrows(1)) dotmatrix_1 (
    .col0(LINEAR[13]), .col1(LINEAR[12]), .col2(LINEAR[11]), .col3(LINEAR[10]), .col4(LINEAR[9]),
    .col5(LINEAR[8]), .col6(LINEAR[7]), .col7(LINEAR[6]), .col8(LINEAR[5]), .col9(LINEAR[4]),
    .col10(LINEAR[3]), .col11(LINEAR[2]), .col12(LINEAR[1]), .col13(LINEAR[0]));
  Hex_Digit_Display hex_digit_display_6 (.value(LINEAR[3:0]));  // open: dp
  assign not_1_out = ~counter_1_q;  // NOT_Gate not_1, 4 bits wide
  Comparator #(.width(4), .mode("unsigned")) comparator_1 (
    .a(counter_1_q), .b(adder_1_out), .eq(STOP));  // open: gt, lt
  and and_2 (LOAD, not_1_out[3], not_1_out[2], not_1_out[1], counter_1_q[0]);
  and and_3 (CLR, not_1_out[3], not_1_out[2], not_1_out[1], not_1_out[0]);
  Adder #(.width(6)) adder_2 (.a(6'b100001), .b({1'b0, MULAW[3:0], 1'b0}), .out(adder_2_out));  // open: cin, cout
  // Shift_Register #(.length(13)) shift_register_1: pin names not known; wires that end beside it: CLR, LOAD, SHIFT, CLK, 1'b0, adder_2_out[0], adder_2_out[1], adder_2_out[2], adder_2_out[3], adder_2_out[4], adder_2_out[5], 1'b0, shift_register_1_p13[0], shift_register_1_p13[1], shift_register_1_p13[2], shift_register_1_p13[3], shift_register_1_p13[4], shift_register_1_p13[5], shift_register_1_p13[6], shift_register_1_p13[7], shift_register_1_p13[8], shift_register_1_p13[9], shift_register_1_p13[10], shift_register_1_p13[11]
  nor nor_1 (SHIFT, STOP, LOAD, CLR);
  Subtractor #(.width(14)) subtractor_1 (
    .a({1'b0, shift_register_1_p13}), .b(14'h21), .out(subtractor_1_out));  // open: bin, bout
  Demultiplexer #(.width(14), .enable("false")) demultiplexer_1 (
    .out0(demultiplexer_1_out0), .out1(demultiplexer_1_out1), .in(subtractor_1_out), .sel(MULAW[7]));
  Multiplexer #(.width(14), .enable("false")) multiplexer_1 (
    .in0(demultiplexer_1_out0), .in1(negator_1_out), .out(LINEAR), .sel(MULAW[7]));
  Negator #(.width(14)) negator_1 (.in(demultiplexer_1_out1), .out(negator_1_out));

  // Notes on the sheet:
  //   CLOCK GENERATION
  //   µ-Law
  //   START / STOP STATE MACHINE
  //   LINEAR OUTPUT
  //   LINEAR VALUE LEFT SHIFT
endmodule
