// Logisim project ShiftAdder.circ as structural Verilog: 1 circuit, main circuit main
module main (
);

  wire adder_1_cout, adder_1_out, and_2_out, and_3_out, CBin, CLK, clock_1_out, CLR, CLR_BTN, CLR_out,
       CYCL_STOP, d_ff_1_q, ENABLE, LOAD, not_1_out, not_2_out, not_3_out, not_4_out, or_1_out, or_3_out,
       s_r_ff_1_q, shift_register_2_p16, shift_register_2_p17, START, SUBTRACT, xor_1_out, xor_2_out;
  wire [3:0] CYCLE_COUNTER_q;
  wire [7:0] A, B;
  wire [8:0] DATA;

  Button u_START (.out(START));
  Button CLEAR (.out(CLR_BTN));
  DipSwitch dipswitch_1 (
    .sw1(A[0]), .sw2(A[1]), .sw3(A[2]), .sw4(A[3]), .sw5(A[4]), .sw6(A[5]), .sw7(A[6]), .sw8(A[7]));
  DipSwitch dipswitch_2 (
    .sw1(B[0]), .sw2(B[1]), .sw3(B[2]), .sw4(B[3]), .sw5(B[4]), .sw6(B[5]), .sw7(B[6]), .sw8(B[7]));
  Clock clock_1 (.out(clock_1_out));
  S_R_Flip_Flop s_r_ff_1 (.S(START), .R(CYCL_STOP), .clk(clock_1_out), .Q(s_r_ff_1_q));  // open: reset, Qn, preset
  LED led_1 (.in(CLK));
  LED led_2 (.in(CLR));
  LED led_3 (.in(LOAD));
  LED led_4 (.in(ENABLE));
  LED led_5 (.in(CYCL_STOP));
  Counter #(.width(4), .max('hf)) CYCLE_COUNTER (
    .clr(or_1_out), .clk(CLK), .Q(CYCLE_COUNTER_q));  // open: load, up, count, D, carry
  or or_1 (or_1_out, CLR_BTN, START);
  DotMatrix #(.matrixcols(9), .matrixrows(1)) dotmatrix_1 (
    .col0(DATA[8]), .col1(DATA[7]), .col2(DATA[6]), .col3(DATA[5]), .col4(DATA[4]), .col5(DATA[3]),
    .col6(DATA[2]), .col7(DATA[1]), .col8(DATA[0]));
  DipSwitch #(.number(2)) Cin_SUB (.sw1(CBin), .sw2(SUBTRACT));
  and and_1 (CLK, clock_1_out, s_r_ff_1_q);
  and STOP (CYCL_STOP, CYCLE_COUNTER_q[3], CYCLE_COUNTER_q[1]);
  not not_1 (not_1_out, CYCLE_COUNTER_q[0]);
  not not_2 (not_2_out, CYCLE_COUNTER_q[1]);
  not not_3 (not_3_out, CYCLE_COUNTER_q[2]);
  not not_4 (not_4_out, CYCLE_COUNTER_q[3]);
  // Shift_Register shift_register_1: pin names not known; wires that end beside it: CLR, LOAD, ENABLE, CLK, 1'b0, A[0], A[1], A[2], A[3], A[4], A[5]
  // Shift_Register shift_register_2: pin names not known; wires that end beside it: A[6], A[7], CLR, LOAD, ENABLE, CLK, 1'b0, B[0], B[1], B[2], B[3], B[4], B[5], B[6], B[7], shift_register_2_p16, shift_register_2_p17
  and u_LOAD (LOAD, CYCLE_COUNTER_q[0], not_2_out, not_3_out, not_4_out);
  and u_CLR (CLR_out, not_1_out, not_2_out, not_3_out, not_4_out);
  or or_2 (CLR, CLR_out, CLR_BTN);
  Adder #(.width(1)) adder_1 (
    .a(shift_register_2_p16), .b(xor_1_out), .out(adder_1_out), .cin(d_ff_1_q), .cout(adder_1_cout));
  xor xor_1 (xor_1_out, SUBTRACT, shift_register_2_p17);
  Hex_Digit_Display hex_digit_display_1 (.value(CYCLE_COUNTER_q));  // open: dp
  nor nor_1 (ENABLE, CLR, LOAD, CYCL_STOP);
  xor xor_2 (xor_2_out, CBin, SUBTRACT);
  buf and_2 (and_2_out, adder_1_cout);  // AND_Gate
  and and_3 (and_3_out, LOAD, xor_2_out);
  or or_3 (or_3_out, and_2_out, and_3_out);
  D_Flip_Flop d_ff_1 (.D(or_3_out), .clk(CLK), .Q(d_ff_1_q), .reset(CLR));  // open: Qn, preset
  // Shift_Register shift_register_3: pin names not known; wires that end beside it: CLR, ENABLE, CLK, adder_1_out, DATA[7], DATA[6], DATA[5], DATA[4], DATA[3], DATA[2], DATA[1], DATA[0]
  xor xor_3 (DATA[8], SUBTRACT, d_ff_1_q);

  // Other names for the same wires on the sheet: SHIFT = ENABLE

  // Notes on the sheet:
  //   DATA A
  //   DATA B
  //   CLOCK GENERATION
  //   DATA OUTPUT
  //   START / STOP STATE CONTROL SECTION
  //   DATA "A" SHIFT IN
  //   DATA "B" SHIFT IN
  //   Carry-Delayed Adder
  //   DATA PARALLEL OUT
endmodule
