// Logisim project ShiftDivider.circ as structural Verilog: 1 circuit, main circuit main
module main (
);

  wire CLK, clock_1_out, CLR, CLR_BTN, comparator_1_eq, comparator_1_gt, ENABLE, LOAD, not_1_out, not_2_out,
       not_3_out, not_4_out, not_5_out, or_1_out, or_2_out, s_r_ff_1_q, SHIFT, START, STOP, SUB, WRITE_DATA,
       WRITE_IMM;
  wire [4:0] counter_1_q;
  wire [7:0] A, B, multiplexer_3_out, or_3_out, Q_IMM_q, QUOTIENT, T_SHIFT;
  wire [14:0] B_SHIFT, multiplexer_1_out, multiplexer_2_out, R_IMM_q, REMAINDER, subtractor_1_out;

  Clock clock_1 (.out(clock_1_out));
  S_R_Flip_Flop s_r_ff_1 (.S(START), .R(STOP), .clk(clock_1_out), .Q(s_r_ff_1_q));  // open: reset, Qn, preset
  LED led_1 (.in(CLR));
  LED led_2 (.in(LOAD));
  LED led_3 (.in(ENABLE));
  LED led_4 (.in(STOP));
  Button u_START (.out(START));
  Button CLEAR (.out(CLR_BTN));
  Register #(.width(15)) R_IMM (.D(REMAINDER), .en(WRITE_IMM), .clk(CLK), .Q(R_IMM_q), .clr(CLR));
  and and_1 (CLK, clock_1_out, s_r_ff_1_q);
  Counter #(.width(5), .max('h1f)) counter_1 (
    .clr(or_1_out), .clk(CLK), .Q(counter_1_q));  // open: load, up, count, D, carry
  or or_1 (or_1_out, START, CLR_BTN);
  Hex_Digit_Display hex_digit_display_1 (.value(A[3:0]));  // open: dp
  Hex_Digit_Display hex_digit_display_2 (.value(A[7:4]));  // open: dp
  DipSwitch dipswitch_1 (
    .sw1(A[7]), .sw2(A[6]), .sw3(A[5]), .sw4(A[4]), .sw5(A[3]), .sw6(A[2]), .sw7(A[1]), .sw8(A[0]));
  Hex_Digit_Display hex_digit_display_3 (.value(B[7:4]));  // open: dp
  Hex_Digit_Display hex_digit_display_4 (.value(B[3:0]));  // open: dp
  DipSwitch dipswitch_2 (
    .sw1(B[7]), .sw2(B[6]), .sw3(B[5]), .sw4(B[4]), .sw5(B[3]), .sw6(B[2]), .sw7(B[1]), .sw8(B[0]));
  Subtractor #(.width(15)) subtractor_1 (
    .a(R_IMM_q), .b(multiplexer_1_out), .out(subtractor_1_out));  // open: bin, bout
  Multiplexer #(.width(15), .enable("false")) multiplexer_1 (
    .in0({15{1'b0}}), .in1(B_SHIFT), .out(multiplexer_1_out), .sel(SUB));
  not not_1 (not_1_out, counter_1_q[0]);
  not not_2 (not_2_out, counter_1_q[1]);
  not not_3 (not_3_out, counter_1_q[2]);
  not not_4 (not_4_out, counter_1_q[3]);
  not not_5 (not_5_out, counter_1_q[4]);
  Multiplexer #(.width(15), .enable("false")) multiplexer_2 (
    .in0(subtractor_1_out), .in1({{7{1'b0}}, A}), .out(multiplexer_2_out), .sel(LOAD));
  Hex_Digit_Display hex_digit_display_5 (.value(QUOTIENT[3:0]));  // open: dp
  Hex_Digit_Display hex_digit_display_6 (.value(QUOTIENT[7:4]));  // open: dp
  and u_STOP (STOP, counter_1_q[4], counter_1_q[1]);
  Register #(.width(15)) u_REMAINDER (.D(multiplexer_2_out), .en(WRITE_DATA), .clk(CLK), .Q(REMAINDER), .clr(CLR));
  DotMatrix #(.matrixcols(8), .matrixrows(1)) dotmatrix_1 (
    .col0(QUOTIENT[7]), .col1(QUOTIENT[6]), .col2(QUOTIENT[5]), .col3(QUOTIENT[4]), .col4(QUOTIENT[3]),
    .col5(QUOTIENT[2]), .col6(QUOTIENT[1]), .col7(QUOTIENT[0]));
  and u_LOAD (LOAD, not_5_out, not_4_out, not_3_out, not_2_out, counter_1_q[0]);
  // Shift_Register shift_register_1: pin names not known; wires that end beside it: not_1_out, CLR, LOAD, SHIFT, CLK, 1'b0, 1'b1, 1'b0, 1'b0, 1'b0, 1'b0, 1'b0, 1'b0, 1'b0, T_SHIFT[7], T_SHIFT[6], T_SHIFT[5], T_SHIFT[4], T_SHIFT[3], T_SHIFT[2], T_SHIFT[1], T_SHIFT[0]
  and u_CLR (CLR, not_5_out, not_4_out, not_3_out, not_2_out, not_1_out);
  Hex_Digit_Display hex_digit_display_7 (.value(REMAINDER[7:4]));  // open: dp
  Hex_Digit_Display hex_digit_display_8 (.value(REMAINDER[3:0]));  // open: dp
  nor nor_1 (ENABLE, CLR, LOAD, STOP);
  DotMatrix #(.matrixcols(8), .matrixrows(1)) dotmatrix_2 (
    .col0(REMAINDER[7]), .col1(REMAINDER[6]), .col2(REMAINDER[5]), .col3(REMAINDER[4]), .col4(REMAINDER[3]),
    .col5(REMAINDER[2]), .col6(REMAINDER[1]), .col7(REMAINDER[0]));
  Decoder #(.enable("false")) decoder_1 (.out0(WRITE_IMM), .out1(WRITE_DATA), .sel(counter_1_q[0]));
  and and_2 (SHIFT, counter_1_q[0], ENABLE);
  Comparator #(.width(15), .mode("unsigned")) comparator_1 (
    .a(REMAINDER), .b(B_SHIFT), .gt(comparator_1_gt), .eq(comparator_1_eq));  // open: lt
  Multiplexer #(.width(8), .enable("false")) multiplexer_3 (
    .in0({8{1'b0}}), .in1(T_SHIFT), .out(multiplexer_3_out), .sel(SUB));
  Register Q_IMM (.D(QUOTIENT), .en(WRITE_IMM), .clk(CLK), .Q(Q_IMM_q), .clr(CLR));
  and and_3 (SUB, WRITE_DATA, or_2_out);
  or or_2 (or_2_out, comparator_1_gt, comparator_1_eq);
  assign or_3_out = multiplexer_3_out | Q_IMM_q;  // OR_Gate or_3, 8 bits wide
  Register u_QUOTIENT (.D(or_3_out), .en(WRITE_DATA), .clk(CLK), .Q(QUOTIENT), .clr(CLR));
  // Shift_Register #(.length(15)) shift_register_2: pin names not known; wires that end beside it: CLR, LOAD, SHIFT, CLK, 1'b0, B[7], B[6], B[5], B[4], B[3], B[2], B[1], B[0], B_SHIFT[14], B_SHIFT[13], B_SHIFT[12], B_SHIFT[11], B_SHIFT[10], B_SHIFT[9], B_SHIFT[8], B_SHIFT[7], B_SHIFT[6], B_SHIFT[5], B_SHIFT[4], B_SHIFT[3]

  // Other names for the same wires on the sheet: A_LOAD[7:0] = A

  // Notes on the sheet:
  //   CLOCK GENERATION
  //   REMAINDER DATA PATH CONTROL & MULTIPLEX
  //   DATA "A"
  //   DATA "B"
  //   START / STOP CONTROL STATE MACHINE
  //   QUOTIENT
  //   QUOTIENT ADD
  //   REMAINDER
  //   QUOTIENT DATA PATH CONTROL & MULTIPLEX
  //   BIT EXPANSION
  //   REMAINDER SUBTRACT
endmodule
