// Logisim project ShiftMultiplier.circ as structural Verilog: 1 circuit, main circuit main
module main (
);

  wire ADD, B_SHIFT, CLK, clock_1_out, CLR, CLR_BTN, ENABLE, LOAD, not_1_out, not_2_out, not_3_out,
       not_4_out, not_5_out, or_1_out, s_r_ff_1_q, SHIFT, START, STOP, WRITE_DATA, WRITE_IMM;
  wire [4:0] counter_1_q;
  wire [7:0] A, B;
  wire [15:0] A_SHIFT, adder_1_out, bit_extender_1_out, DATA, IMM_q, multiplexer_1_out;

  Clock clock_1 (.out(clock_1_out));
  S_R_Flip_Flop s_r_ff_1 (.S(START), .R(STOP), .clk(clock_1_out), .Q(s_r_ff_1_q));  // open: reset, Qn, preset
  LED led_1 (.in(CLR));
  LED led_2 (.in(LOAD));
  LED led_3 (.in(ENABLE));
  LED led_4 (.in(STOP));
  Button u_START (.out(START));
  Button CLEAR (.out(CLR_BTN));
  and and_1 (CLK, clock_1_out, s_r_ff_1_q);
  Counter #(.width(5), .max('h1f)) counter_1 (
    .clr(or_1_out), .clk(CLK), .Q(counter_1_q));  // open: load, up, count, D, carry
  or or_1 (or_1_out, START, CLR_BTN);
  Hex_Digit_Display hex_digit_display_1 (.value(A[3:0]));  // open: dp
  Hex_Digit_Display hex_digit_display_2 (.value(A[7:4]));  // open: dp
  DipSwitch dipswitch_1 (
    .sw1(A[7]), .sw2(A[6]), .sw3(A[5]), .sw4(A[4]), .sw5(A[3]), .sw6(A[2]), .sw7(A[1]), .sw8(A[0]));
  Hex_Digit_Display hex_digit_display_3 (.value(B[7:4]));  // open: dp
  Hex_Digit_Display hex_digit_display_4 (.value(B[3:0]));  // open: dp
  DipSwitch dipswitch_2 (
    .sw1(B[7]), .sw2(B[6]), .sw3(B[5]), .sw4(B[4]), .sw5(B[3]), .sw6(B[2]), .sw7(B[1]), .sw8(B[0]));
  not not_1 (not_1_out, counter_1_q[0]);
  not not_2 (not_2_out, counter_1_q[1]);
  not not_3 (not_3_out, counter_1_q[2]);
  not not_4 (not_4_out, counter_1_q[3]);
  not not_5 (not_5_out, counter_1_q[4]);
  Hex_Digit_Display hex_digit_display_5 (.value(DATA[11:8]));  // open: dp
  Hex_Digit_Display hex_digit_display_6 (.value(DATA[15:12]));  // open: dp
  and u_STOP (STOP, counter_1_q[4], counter_1_q[1]);
  Hex_Digit_Display hex_digit_display_7 (.value(DATA[3:0]));  // open: dp
  Hex_Digit_Display hex_digit_display_8 (.value(DATA[7:4]));  // open: dp
  and u_LOAD (LOAD, not_5_out, not_4_out, not_3_out, not_2_out, counter_1_q[0]);
  DotMatrix #(.matrixcols(16), .matrixrows(1)) dotmatrix_1 (
    .col0(DATA[15]), .col1(DATA[14]), .col2(DATA[13]), .col3(DATA[12]), .col4(DATA[11]), .col5(DATA[10]),
    .col6(DATA[9]), .col7(DATA[8]), .col8(DATA[7]), .col9(DATA[6]), .col10(DATA[5]), .col11(DATA[4]),
    .col12(DATA[3]), .col13(DATA[2]), .col14(DATA[1]), .col15(DATA[0]));
  Multiplexer #(.width(16), .enable("false")) multiplexer_1 (
    .in0({16{1'b0}}), .in1(A_SHIFT), .out(multiplexer_1_out), .sel(ADD));
  Register #(.width(16)) IMM (.D(DATA), .en(WRITE_IMM), .clk(CLK), .Q(IMM_q), .clr(CLR));
  and u_CLR (CLR, not_5_out, not_4_out, not_3_out, not_2_out, not_1_out);
  Adder #(.width(16)) adder_1 (.a(multiplexer_1_out), .b(IMM_q), .out(adder_1_out));  // open: cin, cout
  Decoder #(.enable("false")) decoder_1 (.out0(WRITE_IMM), .out1(WRITE_DATA), .sel(counter_1_q[0]));
  nor nor_1 (ENABLE, CLR, LOAD, STOP);
  Register #(.width(16)) u_DATA (.D(adder_1_out), .en(WRITE_DATA), .clk(CLK), .Q(DATA), .clr(CLR));
  and and_2 (SHIFT, counter_1_q[0], ENABLE);
  and and_3 (ADD, WRITE_DATA, B_SHIFT);
  assign bit_extender_1_out = {{8{1'b0}}, A};  // Bit_Extender bit_extender_1
  // Shift_Register #(.length(16)) shift_register_1: pin names not known; wires that end beside it: CLR, LOAD, SHIFT, CLK, 1'b0, bit_extender_1_out[0], bit_extender_1_out[1], bit_extender_1_out[2], bit_extender_1_out[3], bit_extender_1_out[4], bit_extender_1_out[5], bit_extender_1_out[6], bit_extender_1_out[7], A_SHIFT[0], A_SHIFT[1], A_SHIFT[2], A_SHIFT[3], A_SHIFT[4], A_SHIFT[5], A_SHIFT[6], A_SHIFT[7]
  // Shift_Register shift_register_2: pin names not known; wires that end beside it: bit_extender_1_out[8], bit_extender_1_out[9], bit_extender_1_out[10], bit_extender_1_out[11], bit_extender_1_out[12], bit_extender_1_out[13], bit_extender_1_out[14], bit_extender_1_out[15], CLR, LOAD, SHIFT, CLK, 1'b0, B[7], B[6], B[5], B[4], B[3], B[2], B[1], B[0], A_SHIFT[8], A_SHIFT[9], A_SHIFT[10], A_SHIFT[11], A_SHIFT[12], A_SHIFT[13], A_SHIFT[14], A_SHIFT[15], B_SHIFT

  // Notes on the sheet:
  //   CLOCK GENERATION
  //   DATA "A"
  //   DATA "B"
  //   START / STOP CONTROL STATE MACHINE
  //   OUTPUT
  //   DATA PATH CONTROL & MULTIPLEXER
  //   DATA "A"
  //   DATA "B"
endmodule
