// Logisim project TicTacToe.circ as structural Verilog: 1 circuit, main circuit main
module main (
);

  wire A_EN, A_F, A_FIRST_out, and_7_out, and_8_out, and_9_out, and_12_out, and_14_out, B_EN, B_F,
       B_FIRST_out, CLK, d_ff_1_qn, ENABLE, not_5_out, or_1_out, or_2_out, or_4_out, RST, s_r_ff_2_q,
       s_r_ff_2_qn, TIE;
  wire [1:0] WIN;
  wire [8:0] A_KP, A_REG, and_1_out, and_2_out, and_3_out, and_4_out, and_5_out, and_6_out, and_11_out,
       and_13_out, B_KP, B_REG, not_1_out, not_2_out, not_3_out, not_4_out, not_6_out, not_7_out, or_3_out,
       or_5_out, or_6_out;

  Clock clock_1 (.out(CLK));
  Button button_1 (.out(A_KP[6]));
  Button button_2 (.out(A_KP[7]));
  LED led_1 (.in(A_EN));
  Button button_3 (.out(A_KP[8]));
  Button button_4 (.out(RST));
  Button B_FIRST (.out(B_FIRST_out));
  S_R_Flip_Flop s_r_ff_1 (.S(B_FIRST_out), .R(A_FIRST_out), .clk(CLK), .Q(B_F), .Qn(A_F));  // open: reset, preset
  Button A_FIRST (.out(A_FIRST_out));
  Button button_5 (.out(A_KP[3]));
  Button button_6 (.out(A_KP[4]));
  Button button_7 (.out(A_KP[5]));
  Button button_8 (.out(A_KP[0]));
  Button button_9 (.out(A_KP[1]));
  Button button_10 (.out(A_KP[2]));
  assign and_1_out = B_REG & A_KP;  // AND_Gate and_1, 9 bits wide
  assign and_2_out = A_REG & B_KP;  // AND_Gate and_2, 9 bits wide
  assign not_1_out = ~A_REG;  // NOT_Gate not_1, 9 bits wide
  assign not_2_out = ~and_1_out;  // NOT_Gate not_2, 9 bits wide
  assign and_3_out = not_2_out & A_KP;  // AND_Gate and_3, 9 bits wide
  assign not_3_out = ~B_REG;  // NOT_Gate not_3, 9 bits wide
  assign not_4_out = ~and_2_out;  // NOT_Gate not_4, 9 bits wide
  assign and_4_out = not_4_out & B_KP;  // AND_Gate and_4, 9 bits wide
  Button button_11 (.out(B_KP[6]));
  Button button_12 (.out(B_KP[7]));
  LED led_2 (.in(B_EN));
  Button button_13 (.out(B_KP[8]));
  or or_1 (or_1_out, and_5_out[0], and_5_out[1], and_5_out[2], and_5_out[3], and_5_out[4], and_5_out[5], and_5_out[6], and_5_out[7], and_5_out[8]);
  assign and_5_out = not_1_out & and_3_out;  // AND_Gate and_5, 9 bits wide
  or or_2 (or_2_out, and_6_out[0], and_6_out[1], and_6_out[2], and_6_out[3], and_6_out[4], and_6_out[5], and_6_out[6], and_6_out[7], and_6_out[8]);
  assign and_6_out = not_3_out & and_4_out;  // AND_Gate and_6, 9 bits wide
  Button button_14 (.out(B_KP[3]));
  Button button_15 (.out(B_KP[4]));
  Button button_16 (.out(B_KP[5]));
  assign or_3_out = A_REG | B_REG;  // OR_Gate or_3, 9 bits wide
  S_R_Flip_Flop s_r_ff_2 (
    .S(or_1_out), .R(or_2_out), .clk(CLK), .Q(s_r_ff_2_q), .reset(and_9_out), .Qn(s_r_ff_2_qn),
    .preset(and_8_out));
  Button button_17 (.out(B_KP[0]));
  Button button_18 (.out(B_KP[1]));
  Button button_19 (.out(B_KP[2]));
  // PlaRom #(.\and (16), .outputs(2), .Contents("0*15 2*3 0*12 2*3 0*12 2*3 0*15 2 0 0 2 0 0 2 0*12 2 0 0 2 0 0 2 0*12 2 0 0 2 0 0 2 0*9 2 0*3 2 0*3 2 0*11 2 0 2 0 2 0*8 2*3 0*12 2*3 0*12 2*3 0*15 2 0 0 2 0 0 2 0*12 2 0 0 2 0 0 2 0*12 2 0 0 2 0 0 2 0*9 2 0*3 2 0*3 2 0*11 2 0 2 0 2 0*11 1 0 1 0 1 0 1 0 1 0 1 0 1 0 1 0 0 1 0 1 0 1 0 1 0 1 0 1 0 1 0 1")) WIN_PLA: pin names not known; wires that end beside it: {B_REG, A_REG}, WIN
  and and_7 (and_7_out, or_3_out[0], or_3_out[1], or_3_out[2], or_3_out[3], or_3_out[4], or_3_out[5], or_3_out[6], or_3_out[7], or_3_out[8]);
  and and_8 (and_8_out, B_F, RST);
  and and_9 (and_9_out, A_F, RST);
  not not_5 (not_5_out, or_4_out);
  or or_4 (or_4_out, WIN[0], WIN[1]);
  D_Flip_Flop d_ff_1 (.D(s_r_ff_2_q), .clk(CLK), .Q(B_EN), .Qn(d_ff_1_qn));  // open: preset, reset
  D_Flip_Flop d_ff_2 (.D(s_r_ff_2_qn), .clk(CLK), .Q(A_EN));  // open: Qn, preset, reset
  nor nor_1 (ENABLE, and_7_out, or_4_out);
  and and_10 (TIE, and_7_out, not_5_out);
  // RGBLED rgbled_1: pin names not known; wires that end beside it: B_REG[6], A_REG[6]
  // RGBLED rgbled_2: pin names not known; wires that end beside it: B_REG[7], A_REG[7]
  // RGBLED rgbled_3: pin names not known; wires that end beside it: B_REG[8], A_REG[8]
  // RGBLED rgbled_4: pin names not known; wires that end beside it: B_REG[3], A_REG[3]
  // RGBLED rgbled_5: pin names not known; wires that end beside it: B_REG[4], A_REG[4]
  // RGBLED rgbled_6: pin names not known; wires that end beside it: B_REG[5], A_REG[5]
  // RGBLED rgbled_7: pin names not known; wires that end beside it: B_REG[0], A_REG[0]
  // RGBLED rgbled_8: pin names not known; wires that end beside it: B_REG[1], A_REG[1]
  // RGBLED rgbled_9: pin names not known; wires that end beside it: B_REG[2], A_REG[2]
  assign not_6_out = ~B_REG;  // NOT_Gate not_6, 9 bits wide
  assign or_5_out = A_REG | and_11_out;  // OR_Gate or_5, 9 bits wide
  assign and_11_out = not_6_out & A_KP;  // AND_Gate and_11, 9 bits wide
  and and_12 (and_12_out, A_EN, ENABLE);
  assign or_6_out = B_REG | and_13_out;  // OR_Gate or_6, 9 bits wide
  assign not_7_out = ~A_REG;  // NOT_Gate not_7, 9 bits wide
  assign and_13_out = not_7_out & B_KP;  // AND_Gate and_13, 9 bits wide
  and and_14 (and_14_out, B_EN, ENABLE);
  LED A (.in(WIN[1]));
  Register #(.width(9)) register_1 (.D(or_5_out), .en(and_12_out), .clk(CLK), .Q(A_REG), .clr(RST));
  Register #(.width(9)) register_2 (.D(or_6_out), .en(and_14_out), .clk(CLK), .Q(B_REG), .clr(RST));
  LED u_TIE (.in(TIE));
  LED B (.in(WIN[0]));

  // Notes on the sheet:
  //   GLOBAL RESET
  //   WHO FIRST
  //   KEYPAD A
  //   KEYPAD B
  //   WIN / TIE CONDITION
  //   KEYPAD CONTROL
  //   RESULT
  //   REGISTER A
  //   REGISTER B
  //   WIN OR TIE
endmodule
